# Fritzing sketch arduino_receiver (saved by Fritzing 0.9.3b)

parts:
  U1 = Voltage Regulator -- 3.3 V -- LM1117
  Onderdeel1 = Arduino Uno (Rev3)
  Onderdeel2 = NRF24L01+ Breakout Board

nets:
  GND: U1.GND, Onderdeel1.GND, Onderdeel2.GND
  N1: U1.OUT, Onderdeel2.VCC
  N2: U1.IN, Onderdeel1.5V
  N3: Onderdeel1.D8, Onderdeel2.CS
  N4: Onderdeel1.D11_PWM/MOSI, Onderdeel2.MOSI
  N5: Onderdeel1.D12/MISO, Onderdeel2.MISO
  N6: Onderdeel1.D13/SCK, Onderdeel2.SCK
  N7: Onderdeel1.D7, Onderdeel2.CE

custom parts:
  Voltage Regulator -- 3.3 V -- LM1117: LM1117-3.3 Voltage regulator, 3.3 V output. Note that the pinout order is not the same as LM7805 or LM7833.
