# Fritzing sketch arduino_sender (saved by Fritzing 0.9.3b)

parts:
  U1 = Voltage Regulator -- 3.3 V -- LM1117
  Onderdeel1 = Arduino Uno (Rev3)
  Onderdeel2 = NRF24L01+ Breakout Board
  DS1 = DS18B20 1-Wire Temperature Sensor [part_number=DS18B20]
  R1 = Resistor [tolerance=±5% resistance=4.7k package=THT]
  LED1 = LED - 5mm [color="Green (565nm)" package="5 mm [THT]"]
  LED2 = LED - 5mm [color="Red (633nm)" package="5 mm [THT]"]

nets:
  GND: U1.GND, Onderdeel1.GND, Onderdeel2.GND, DS1.GND, LED1.cathode, LED2.cathode
  N1: U1.OUT, Onderdeel2.VCC
  5V: U1.IN, Onderdeel1.5V, DS1.VDD, R1.Pin_1
  N2: Onderdeel1.D8, Onderdeel2.CS
  N3: Onderdeel1.D11_PWM/MOSI, Onderdeel2.MOSI
  N4: Onderdeel1.D12/MISO, Onderdeel2.MISO
  N5: Onderdeel1.D13/SCK, Onderdeel2.SCK
  N6: Onderdeel1.D2, DS1.DQ, R1.Pin_0
  N7: Onderdeel1.D3_PWM, LED1.anode
  N8: Onderdeel1.D4, LED2.anode
  N9: Onderdeel1.D7, Onderdeel2.CE

custom parts:
  Voltage Regulator -- 3.3 V -- LM1117: LM1117-3.3 Voltage regulator, 3.3 V output. Note that the pinout order is not the same as LM7805 or LM7833.
